// Logisim project 1bit-half-subtractor.circ as structural Verilog: 1 circuit, main circuit main
module main (
  input  A,
  input  B,
  output DIFFERENCE,
  output BORROW
);

  wire not_1_out;

  not not_1 (not_1_out, A);
  xor xor_1 (DIFFERENCE, A, B);
  and and_1 (BORROW, not_1_out, B);
endmodule
