// Logisim project full_adder(optimised).circ as structural Verilog: 2 circuits, main circuit ha
module main (
  input  A,
  input  B,
  output SUM,
  output CARRY
);

  xor xor_1 (SUM, A, B);
  and and_1 (CARRY, B, A);
endmodule

module ha (
  input  A,
  input  B,
  input  Cin,
  output SUM,
  output CARRY
);

  wire main_1_carry, main_1_sum, main_2_carry;

  main main_1 (.A(A), .B(B), .SUM(main_1_sum), .CARRY(main_1_carry));
  main main_2 (.A(main_1_sum), .B(Cin), .SUM(SUM), .CARRY(main_2_carry));
  xor xor_1 (CARRY, main_2_carry, main_1_carry);
endmodule
