// Logisim project full_subtractor(optimised).circ as structural Verilog: 2 circuits, main circuit hs
module main (
  input  A,
  input  B,
  output DIFFERENCE,
  output BORROW
);

  wire not_1_out;

  not not_1 (not_1_out, A);
  xor xor_1 (DIFFERENCE, A, B);
  and and_1 (BORROW, not_1_out, B);
endmodule

module hs (
  input  A,
  input  B,
  input  Bin,
  output DIFFERENCE,
  output BORROW
);

  wire main_1_borrow, main_1_difference, main_2_borrow;

  main main_1 (.A(A), .B(B), .DIFFERENCE(main_1_difference), .BORROW(main_1_borrow));
  main main_2 (.A(main_1_difference), .B(Bin), .DIFFERENCE(DIFFERENCE), .BORROW(main_2_borrow));
  or or_1 (BORROW, main_2_borrow, main_1_borrow);
endmodule
