// Logisim project 2x+y.circ as structural Verilog: 1 circuit, main circuit main
module main (
  input  [7:0] X,
  input  [7:0] Y,
  output [7:0] RESULT
);

  wire [7:0] multiplier_1_out;

  Multiplier multiplier_1 (.a(X), .b(8'h2), .out(multiplier_1_out));  // open: cin, cout
  Adder adder_1 (.a(multiplier_1_out), .b(Y), .out(RESULT));  // open: cin, cout
endmodule
