// Logisim project 2x.circ as structural Verilog: 1 circuit, main circuit main
module main (
  input  [7:0] in_1,
  output [7:0] RESULT
);

  Multiplier multiplier_1 (.a(8'h2), .b(in_1), .out(RESULT));  // open: cin, cout
endmodule
