// Logisim project Average.circ as structural Verilog: 1 circuit, main circuit main
module main (
  input  [7:0] X,
  input  [7:0] Y,
  output [7:0] AVERAGE
);

  wire [7:0] adder_1_out;

  Adder adder_1 (.a(X), .b(Y), .out(adder_1_out));  // open: cin, cout
  Shifter #(.shift("lr")) shifter_1 (.in(adder_1_out), .\dist (3'b001), .out(AVERAGE));
endmodule
