// Logisim project Product.circ as structural Verilog: 2 circuits, main circuit main
module main (
  input  [7:0] X,
  input  [7:0] Y,
  output [7:0] X_Y
);

  Multiplier multiplier_1 (.a(X), .b(Y), .out(X_Y));  // open: cin, cout
endmodule

module ax_y (
  input  [7:0] A,
  input  [7:0] X,
  input  [7:0] Y,
  output [7:0] out_4
);

  wire [7:0] main_1_x_y;

  main main_1 (.X(A), .Y(X), .X_Y(main_1_x_y));
  Adder adder_1 (.a(main_1_x_y), .b(Y), .out(out_4));  // open: cin, cout
endmodule
