// Logisim project x^2.circ as structural Verilog: 1 circuit, main circuit main
module main (
  input  [7:0] X,
  output [7:0] X_2
);

  Multiplier multiplier_1 (.a(X), .b(X), .out(X_2));  // open: cin, cout
endmodule
