// Logisim project x^6.circ as structural Verilog: 2 circuits, main circuit x^6
module main (
  input  [7:0] X,
  output [7:0] X_2
);

  Multiplier multiplier_1 (.a(X), .b(X), .out(X_2));  // open: cin, cout
endmodule

module x_6 (
  input  [7:0] in_1,
  output [7:0] out_2
);

  wire [7:0] main_1_x_2, main_2_x_2, main_3_x_2, multiplier_1_out;

  main main_1 (.X(in_1), .X_2(main_1_x_2));
  main main_2 (.X(in_1), .X_2(main_2_x_2));
  main main_3 (.X(in_1), .X_2(main_3_x_2));
  Multiplier multiplier_1 (.a(main_1_x_2), .b(main_2_x_2), .out(multiplier_1_out));  // open: cin, cout
  Multiplier multiplier_2 (.a(multiplier_1_out), .b(main_3_x_2), .out(out_2));  // open: cin, cout
endmodule
