// Logisim project 4x'.circ as structural Verilog: 2 circuits, main circuit 4x'
module main (
  input  [7:0] in_1,
  output [7:0] out_2
);

  assign out_2 = ~in_1;  // NOT_Gate not_1, 8 bits wide
endmodule

module _4x (
  input  [7:0] X,
  output [7:0] out_2
);

  wire [7:0] multiplier_1_out;

  Multiplier multiplier_1 (.a(X), .b(8'h4), .out(multiplier_1_out));  // open: cin, cout
  main main_1 (.in_1(multiplier_1_out), .out_2(out_2));
endmodule
