// Logisim project average.circ as structural Verilog: 1 circuit, main circuit main
module main (
  input  [7:0] A,
  input  [7:0] B,
  input  [7:0] C,
  input  [7:0] D,
  output [7:0] out_5
);

  wire [7:0] adder_1_out, adder_2_out, adder_3_out;

  Adder adder_1 (.a(A), .b(B), .out(adder_1_out));  // open: cin, cout
  Adder adder_2 (.a(C), .b(D), .out(adder_2_out));  // open: cin, cout
  Adder adder_3 (.a(adder_1_out), .b(adder_2_out), .out(adder_3_out));  // open: cin, cout
  Shifter #(.shift("lr")) shifter_1 (.in(adder_3_out), .\dist (3'b010), .out(out_5));
endmodule
