// Logisim project x^2+y^2+2xy.circ as structural Verilog: 2 circuits, main circuit x^2+2xy+y^2
module main (
  input  [7:0] X,
  output [7:0] X_2
);

  Multiplier multiplier_1 (.a(X), .b(X), .out(X_2));  // open: cin, cout
endmodule

module x_2_2xy_y_2 (
  input  [7:0] X,
  input  [7:0] Y,
  output [7:0] out_3
);

  wire [7:0] adder_1_out;

  Adder adder_1 (.a(X), .b(Y), .out(adder_1_out));  // open: cin, cout
  main main_1 (.X(adder_1_out), .X_2(out_3));
endmodule
