// Logisim project 4_Bit_Half_Adder.circ as structural Verilog: 3 circuits, main circuit HA
module main (
  input  A,
  input  B,
  output SUM,
  output CARRY
);

  xor xor_1 (SUM, A, B);
  and and_1 (CARRY, B, A);
endmodule

module HA (
  input  A0,
  input  B0,
  input  A1,
  input  A2,
  input  A3,
  input  B1,
  input  B2,
  input  B3,
  output S0,
  output S1,
  output S2,
  output S3,
  output C0,
  output C1,
  output C2,
  output C3
);

  main main_1 (.A(A0), .B(B0), .SUM(S0), .CARRY(C0));
  main main_2 (.A(A1), .B(B1), .SUM(S1), .CARRY(C1));
  main main_3 (.A(A2), .B(B2), .SUM(S2), .CARRY(C2));
  main main_4 (.A(A3), .B(B3), .SUM(S3), .CARRY(C3));
endmodule

module _8_bit_half_adder (
  input  in_1,
  input  in_2,
  input  in_3,
  input  in_4,
  input  in_5,
  input  in_6,
  input  in_7,
  input  in_8,
  output out_9,
  output out_10,
  output out_11,
  output out_12
);

  HA ha_1 (
    .A0(in_1), .B0(in_2), .A1(in_3), .A2(in_5), .A3(in_6), .B1(in_4), .B2(in_7), .B3(in_8), .S0(out_9),
    .S1(out_11), .C0(out_10), .C1(out_12));  // open: S2, S3, C2, C3
endmodule
