// Logisim project 4_Bit_Half_Subtractor.circ as structural Verilog: 2 circuits, main circuit HS
module main (
  input  A,
  input  B,
  output DIFFERENCE,
  output BORROW
);

  wire not_1_out;

  not not_1 (not_1_out, A);
  xor xor_1 (DIFFERENCE, A, B);
  and and_1 (BORROW, not_1_out, B);
endmodule

module HS (
  input  A0,
  input  A1,
  input  B0,
  input  A3,
  input  A2,
  input  B1,
  input  B2,
  input  B3,
  output D0,
  output D1,
  output D2,
  output D3,
  output out_13,
  output out_14,
  output Br1,
  output Br2
);

  main main_1 (.A(A0), .B(B0), .DIFFERENCE(D0), .BORROW(out_14));
  main main_2 (.A(A1), .B(B1), .DIFFERENCE(D1), .BORROW(Br1));
  main main_3 (.A(A2), .B(B2), .DIFFERENCE(D2), .BORROW(Br2));
  main main_4 (.A(A3), .B(B3), .DIFFERENCE(D3), .BORROW(out_13));

  // Notes on the sheet:
  //   Br0
  //   Br3
endmodule
