// Logisim project 4_bit_full_adder.circ as structural Verilog: 3 circuits, main circuit FA
module main (
  input  A,
  input  B,
  input  Cin,
  output SUM,
  output CARRY
);

  wire and_1_out, and_2_out, xor_1_out;

  xor xor_1 (xor_1_out, A, B);
  and and_1 (and_1_out, Cin, xor_1_out);
  and and_2 (and_2_out, B, A);
  xor xor_2 (SUM, xor_1_out, Cin);
  or or_1 (CARRY, and_1_out, and_2_out);
endmodule

module FA (
  input  A0,
  input  B0,
  input  A1,
  input  A2,
  input  Cin,
  input  A3,
  input  B1,
  input  B2,
  input  B3,
  output S0,
  output S1,
  output S2,
  output S3,
  output Cout
);

  wire main_1_carry, main_2_carry, main_3_carry;

  main main_1 (.A(A0), .B(B0), .Cin(Cin), .SUM(S0), .CARRY(main_1_carry));
  main main_2 (.A(A1), .B(B1), .Cin(main_1_carry), .SUM(S1), .CARRY(main_2_carry));
  main main_3 (.A(A2), .B(B2), .Cin(main_2_carry), .SUM(S2), .CARRY(main_3_carry));
  main main_4 (.A(A3), .B(B3), .Cin(main_3_carry), .SUM(S3), .CARRY(Cout));

  // Notes on the sheet:
  //   LSB
  //   Example: 1011 + 1100 = 10111
  //   MSB
endmodule

module _8Bit (
  input  A3,
  input  B3,
  input  A2,
  input  B2,
  input  A1,
  input  B1,
  input  A0,
  input  B0,
  input  Cin,
  output out_10,
  output out_11,
  output out_12,
  output out_13,
  output out_14,
  output out_15,
  output out_16,
  output out_17
);

  wire fa_1_s0;

  FA fa_1 (
    .A0(A3), .B0(B3), .A1(A2), .A2(B2), .Cin(A1), .A3(B1), .B1(A0), .B2(B0), .B3(Cin), .S0(fa_1_s0),
    .S1(out_14), .S2(out_15), .S3(out_16), .Cout(out_17));
  FA fa_2 (.B3(fa_1_s0));  // open: A0, B0, A1, A2, Cin, A3, B1, B2, S0, S1, S2, S3, Cout
endmodule
