// Logisim project 4_bit_full_subtractor.circ as structural Verilog: 2 circuits, main circuit FS
module main (
  input  A,
  input  B,
  input  Bin,
  output DIFFERENCE,
  output BORROW
);

  wire and_1_out, and_2_out, not_1_out, not_2_out, xor_1_out;

  xor xor_1 (xor_1_out, A, B);
  not not_1 (not_1_out, A);
  not not_2 (not_2_out, xor_1_out);
  xor xor_2 (DIFFERENCE, xor_1_out, Bin);
  and and_1 (and_1_out, not_2_out, Bin);
  and and_2 (and_2_out, not_1_out, B);
  or or_1 (BORROW, and_1_out, and_2_out);
endmodule

module FS (
  input  A0,
  input  B0,
  input  A1,
  input  A2,
  input  A3,
  input  Bin,
  input  B2,
  input  B3,
  input  B1,
  output D0,
  output D1,
  output D2,
  output D3,
  output Bout
);

  wire main_1_borrow, main_2_borrow, main_3_borrow;

  main main_1 (.A(A0), .B(B0), .Bin(Bin), .DIFFERENCE(D0), .BORROW(main_1_borrow));
  main main_2 (.A(A1), .B(B1), .Bin(main_1_borrow), .DIFFERENCE(D1), .BORROW(main_2_borrow));
  main main_3 (.A(A2), .B(B2), .Bin(main_2_borrow), .DIFFERENCE(D2), .BORROW(main_3_borrow));
  main main_4 (.A(A3), .B(B3), .Bin(main_3_borrow), .DIFFERENCE(D3), .BORROW(Bout));

  // Notes on the sheet:
  //   Example: 1101-0100=1001
endmodule
