// Logisim project 8_bit_full_adder.circ as structural Verilog: 3 circuits, main circuit 8_bit_full_adder
module main (
  input  A,
  input  B,
  input  Cin,
  output SUM,
  output CARRY
);

  wire and_1_out, and_2_out, xor_1_out;

  xor xor_1 (xor_1_out, A, B);
  and and_1 (and_1_out, Cin, xor_1_out);
  and and_2 (and_2_out, B, A);
  xor xor_2 (SUM, xor_1_out, Cin);
  or or_1 (CARRY, and_1_out, and_2_out);
endmodule

module FA (
  input  A0,
  input  B0,
  input  A1,
  input  A2,
  input  Cin,
  input  A3,
  input  B1,
  input  B2,
  input  B3,
  output S0,
  output S1,
  output S2,
  output S3,
  output Cout
);

  wire main_1_carry, main_2_carry, main_3_carry;

  main main_1 (.A(A0), .B(B0), .Cin(Cin), .SUM(S0), .CARRY(main_1_carry));
  main main_2 (.A(A1), .B(B1), .Cin(main_1_carry), .SUM(S1), .CARRY(main_2_carry));
  main main_3 (.A(A2), .B(B2), .Cin(main_2_carry), .SUM(S2), .CARRY(main_3_carry));
  main main_4 (.A(A3), .B(B3), .Cin(main_3_carry), .SUM(S3), .CARRY(Cout));

  // Notes on the sheet:
  //   LSB
  //   Example: 1011 + 1100 = 10111
  //   MSB
endmodule

module _8_bit_full_adder (
  input  A0,
  input  B0,
  input  A1,
  input  A4,
  input  B1,
  input  B4,
  input  A2,
  input  A5,
  input  B2,
  input  B5,
  input  A6,
  input  A3,
  input  B6,
  input  B3,
  input  A7,
  input  B7,
  input  Cin,
  output S0,
  output S1,
  output S2,
  output S3,
  output S4,
  output S5,
  output S6,
  output S7,
  output Cout
);

  wire fa_1_cout;

  FA fa_1 (
    .A0(A0), .B0(B0), .A1(A1), .A2(A2), .Cin(Cin), .A3(A3), .B1(B1), .B2(B2), .B3(B3), .S0(S0), .S1(S1),
    .S2(S2), .S3(S3), .Cout(fa_1_cout));
  FA fa_2 (
    .A0(A4), .B0(B4), .A1(A5), .A2(A6), .Cin(fa_1_cout), .A3(A7), .B1(B5), .B2(B6), .B3(B7), .S0(S4),
    .S1(S5), .S2(S6), .S3(S7), .Cout(Cout));
endmodule
