// Logisim project 8_bit_full_subtractor.circ as structural Verilog: 3 circuits, main circuit 8_bit_full_subtractor
module main (
  input  A,
  input  B,
  input  Bin,
  output DIFFERENCE,
  output BORROW
);

  wire and_1_out, and_2_out, not_1_out, not_2_out, xor_1_out;

  xor xor_1 (xor_1_out, A, B);
  not not_1 (not_1_out, A);
  not not_2 (not_2_out, xor_1_out);
  xor xor_2 (DIFFERENCE, xor_1_out, Bin);
  and and_1 (and_1_out, not_2_out, Bin);
  and and_2 (and_2_out, not_1_out, B);
  or or_1 (BORROW, and_1_out, and_2_out);
endmodule

module FS (
  input  A0,
  input  B0,
  input  A1,
  input  A2,
  input  A3,
  input  Bin,
  input  B2,
  input  B3,
  input  B1,
  output D0,
  output D1,
  output D2,
  output D3,
  output Bout
);

  wire main_1_borrow, main_2_borrow, main_3_borrow;

  main main_1 (.A(A0), .B(B0), .Bin(Bin), .DIFFERENCE(D0), .BORROW(main_1_borrow));
  main main_2 (.A(A1), .B(B1), .Bin(main_1_borrow), .DIFFERENCE(D1), .BORROW(main_2_borrow));
  main main_3 (.A(A2), .B(B2), .Bin(main_2_borrow), .DIFFERENCE(D2), .BORROW(main_3_borrow));
  main main_4 (.A(A3), .B(B3), .Bin(main_3_borrow), .DIFFERENCE(D3), .BORROW(Bout));

  // Notes on the sheet:
  //   Example: 1101-0100=1001
endmodule

module _8_bit_full_subtractor (
  input  A0,
  input  B0,
  input  A1,
  input  A4,
  input  B1,
  input  B4,
  input  A2,
  input  A5,
  input  B2,
  input  B5,
  input  A6,
  input  A3,
  input  B6,
  input  B3,
  input  A7,
  input  B7,
  input  Bin,
  output D0,
  output D1,
  output D2,
  output D3,
  output D4,
  output D5,
  output D6,
  output D7,
  output Bout
);

  wire fs_1_bout;

  FS fs_1 (
    .A0(A0), .B0(B0), .A1(A1), .A2(A2), .A3(A3), .Bin(Bin), .B2(B2), .B3(B3), .B1(B1), .D0(D0), .D1(D1),
    .D2(D2), .D3(D3), .Bout(fs_1_bout));
  FS fs_2 (
    .A0(A4), .B0(B4), .A1(A5), .A2(A6), .A3(A7), .Bin(fs_1_bout), .B2(B6), .B3(B7), .B1(B5), .D0(D4),
    .D1(D5), .D2(D6), .D3(D7), .Bout(Bout));
endmodule
