// Logisim project 8_bit_half_adder.circ as structural Verilog: 3 circuits, main circuit 8_bit_half_adder
module main (
  input  A,
  input  B,
  output SUM,
  output CARRY
);

  xor xor_1 (SUM, A, B);
  and and_1 (CARRY, B, A);
endmodule

module HA (
  input  A0,
  input  B0,
  input  A1,
  input  A2,
  input  A3,
  input  B1,
  input  B2,
  input  B3,
  output S0,
  output S1,
  output S2,
  output S3,
  output C0,
  output C1,
  output C2,
  output C3
);

  main main_1 (.A(A0), .B(B0), .SUM(S0), .CARRY(C0));
  main main_2 (.A(A1), .B(B1), .SUM(S1), .CARRY(C1));
  main main_3 (.A(A2), .B(B2), .SUM(S2), .CARRY(C2));
  main main_4 (.A(A3), .B(B3), .SUM(S3), .CARRY(C3));
endmodule

module _8_bit_half_adder (
  input  A4,
  input  A0,
  input  B4,
  input  B0,
  input  A5,
  input  A1,
  input  B5,
  input  B1,
  input  A6,
  input  A2,
  input  B6,
  input  B2,
  input  A7,
  input  A3,
  input  B7,
  input  B3,
  output S4,
  output S0,
  output C4,
  output C0,
  output S5,
  output S1,
  output C5,
  output C1,
  output S6,
  output S2,
  output C6,
  output C2,
  output S7,
  output S3,
  output C7,
  output C3
);

  HA ha_1 (
    .A0(A0), .B0(B0), .A1(A1), .A2(A2), .A3(A3), .B1(B1), .B2(B2), .B3(B3), .S0(S0), .S1(S1), .S2(S2),
    .S3(S3), .C0(C0), .C1(C1), .C2(C1), .C3(C3));
  HA ha_2 (
    .A0(A4), .B0(B4), .A1(A5), .A2(A6), .A3(A7), .B1(B5), .B2(B6), .B3(B7), .S0(S4), .S1(S5), .S2(S6),
    .S3(S7), .C0(C4), .C1(C5), .C2(C6), .C3(C7));

  assign C2 = C1;
endmodule
