// Logisim project 8_bit_half_subtractor.circ as structural Verilog: 3 circuits, main circuit 8_bit_half_subtractor
module main (
  input  A,
  input  B,
  output DIFFERENCE,
  output BORROW
);

  wire not_1_out;

  not not_1 (not_1_out, A);
  xor xor_1 (DIFFERENCE, A, B);
  and and_1 (BORROW, not_1_out, B);
endmodule

module HS (
  input  A0,
  input  A1,
  input  B0,
  input  A3,
  input  A2,
  input  B1,
  input  B2,
  input  B3,
  output D0,
  output D1,
  output D2,
  output D3,
  output Br3,
  output Br0,
  output Br1,
  output Br2
);

  main main_1 (.A(A0), .B(B0), .DIFFERENCE(D0), .BORROW(Br0));
  main main_2 (.A(A1), .B(B1), .DIFFERENCE(D1), .BORROW(Br1));
  main main_3 (.A(A2), .B(B2), .DIFFERENCE(D2), .BORROW(Br2));
  main main_4 (.A(A3), .B(B3), .DIFFERENCE(D3), .BORROW(Br3));
endmodule

module _8_bit_half_subtractor (
  input  A4,
  input  A0,
  input  B4,
  input  B0,
  input  A5,
  input  A1,
  input  B5,
  input  B1,
  input  A6,
  input  A2,
  input  B6,
  input  B2,
  input  A7,
  input  A3,
  input  B7,
  input  B3,
  output D4,
  output D0,
  output Br4,
  output Br0,
  output D5,
  output D1,
  output Br5,
  output Br1,
  output D6,
  output D2,
  output Br6,
  output Br2,
  output D7,
  output D3,
  output Br7,
  output Br3
);

  HS hs_1 (
    .A0(A0), .A1(A1), .B0(B0), .A3(A3), .A2(A2), .B1(B1), .B2(B2), .B3(B3), .D0(D0), .D1(D1), .D2(D2),
    .D3(D3), .Br3(Br3), .Br0(Br0), .Br1(Br1), .Br2(Br2));
  HS hs_2 (
    .A0(A4), .A1(A5), .B0(B4), .A3(A7), .A2(A6), .B1(B5), .B2(B6), .B3(B7), .D0(D4), .D1(D5), .D2(D6),
    .D3(D7), .Br3(Br7), .Br0(Br4), .Br1(Br5), .Br2(Br6));
endmodule
